# Fritzing sketch Untitled Sketch (saved by Fritzing 0.9.3b)
perfboards: 1

parts:
  WeMos_D1_Mini1 = WeMos D1 Mini
  PIR1 = PIR sensor
  DHT1 = DHT11 Humitidy and Temperature Sensor
  R2 = Resistor [tolerance=±5% resistance=220 package=THT]
  R3 = Photocell (LDR) [package=THT]
  R4 = Resistor [tolerance=±5% resistance=220 package=THT]
  C1 = Tantalum Capacitor [capacitance=1μF package="100 mil [THT, tantalum]"]  # not connected
  S1 = Pushbutton [package=THT]

nets (from the schematic view):
  N1: WeMos_D1_Mini1.3V3, R3.pin_0
  5V: WeMos_D1_Mini1.5V, PIR1.VDD, DHT1.VDD, R2.Pin_1
  N2: WeMos_D1_Mini1.A0, R3.pin_1, R4.Pin_1
  N3: WeMos_D1_Mini1.D3, S1.leg0
  N4: WeMos_D1_Mini1.D4, PIR1.SIG
  N5: WeMos_D1_Mini1.D6, DHT1.DATA, R2.Pin_0
  GND: PIR1.GND, DHT1.GND, R4.Pin_0, S1.leg1

custom parts:
  DHT11 Humitidy and Temperature Sensor: DHT11 Humidity and Temperature Sensor
